// Logisim project z80.circ as structural Verilog: 8 circuits, main circuit test
module test (
  input  [7:0] in_1,
  input  [7:0] in_2,
  input  in_3,
  input  in_4,
  input  in_5,
  input  in_6,
  input  [7:0] in_7,
  input  [7:0] in_8
);

  wire button_1_out, button_2_out;
  wire [7:0] register_2_q;
  wire [31:0] rom_1_data;

  IDynamicMemories_F23 idynamicmemories_f23_1 ();  // open: neg_RFSH, neg_MREQ, A12, A11_A0, D7_D0, neg_WR
  Button button_1 (.out(button_1_out));
  Register register_1 (
    .D({in_4, in_3, in_6, {2{in_5}}, in_6, in_4, in_3}), .en(button_1_out), .clk(button_1_out));  // open: Q, clr
  ROM #(.dataWidth(32)) rom_1 (.addr(in_8), .data(rom_1_data));
  Button button_2 (.out(button_2_out));
  Register register_2 (.D(in_1), .en(button_2_out), .clk(button_2_out), .Q(register_2_q));  // open: clr
  // Probe on rom_1_data
  // Probe on register_2_q

  // Notes on the sheet:
  //   contents of rom_1 (hex, n*v repeats v):
  //   432423 1 0 0 0 222 3 6*0 445 4*0 32214 0 0 0 41242145 22*0 5
endmodule

module databus8 (
  input  [7:0] in_1
);
endmodule

module IDynamicMemories_F23 (
  input  neg_RFSH,
  input  neg_MREQ,
  input  A12,
  input  [11:0] A11_A0,
  input  [7:0] D7_D0,
  input  neg_WR
);

  wire and_1_out, and_2_out, and_3_out, button_1_out, clk, or_1_out, or_2_out, Read, Write;
  wire [7:0] controlled_buffer_2_out, controlled_buffer_3_out;

  Clock clock_1 (.out(clk));
  Button button_1 (.out(button_1_out));
  Controlled_Buffer controlled_buffer_1 ();  // open: in, out, en
  Controlled_Inverter controlled_inverter_1 ();  // open: in, out, en
  assign controlled_buffer_2_out = Write ? D7_D0 : 8'bz;  // Controlled_Buffer controlled_buffer_2
  assign controlled_buffer_3_out = Read ? controlled_buffer_2_out : 8'bz;  // Controlled_Buffer controlled_buffer_3
  // Probe on controlled_buffer_3_out
  D_Flip_Flop d_ff_1 (.D(neg_WR), .clk(clk), .Q(Write), .Qn(Read));  // open: preset, reset
  not not_1 (neg_MREQ, A12);
  and and_1 (and_1_out, ~neg_RFSH, ~neg_MREQ);  // AND_Gate
  and and_2 (and_2_out, ~neg_MREQ, ~A12);  // AND_Gate
  and and_3 (and_3_out, ~neg_MREQ, ~neg_MREQ);  // AND_Gate
  or or_1 (or_1_out, and_1_out, and_2_out);
  or or_2 (or_2_out, and_1_out, and_3_out);
  RAM #(.addrWidth(12), .clearpin("true"), .databus("bidir")) ram_1 (
    .addr(A11_A0), .we(Write), .oe(Read), .clk(clk), .data(controlled_buffer_2_out), .clr(or_2_out));
  RAM #(.addrWidth(12), .clearpin("true"), .databus("bidir")) ram_2 (
    .addr(A11_A0), .we(Write), .oe(Read), .clk(clk), .data(controlled_buffer_2_out), .clr(or_1_out));
endmodule

module WaitStateM1 (
  input  negM1,
  output negWAIT
);

  wire CLK_out, d_ff_2_q, not_1_out, not_2_out, not_3_out, not_4_out;

  Clock CLK (.out(CLK_out));
  not not_1 (not_1_out, d_ff_2_q);
  D_Flip_Flop d_ff_1 (.D(negM1), .clk(CLK_out), .Q(negWAIT), .preset(not_1_out), .reset(not_2_out));  // open: Qn
  not not_2 (not_2_out, 1'b1);
  not not_3 (not_3_out, 1'b1);
  D_Flip_Flop d_ff_2 (.D(negWAIT), .clk(CLK_out), .Q(d_ff_2_q), .preset(not_3_out), .reset(not_4_out));  // open: Qn
  not not_4 (not_4_out, 1'b1);
endmodule

module WaitStateAnyMemory (
  input  negMREQ,
  output negWAIT
);

  wire CLK_out, d_ff_1_q, d_ff_1_qn, d_ff_2_q, not_1_out, not_2_out, not_3_out, not_4_out;

  Clock CLK (.out(CLK_out));
  not not_1 (not_1_out, 1'b1);
  D_Flip_Flop d_ff_1 (.D(negMREQ), .clk(CLK_out), .Q(d_ff_1_q), .Qn(d_ff_1_qn), .preset(not_1_out), .reset(not_2_out));
  not not_2 (not_2_out, 1'b1);
  not not_3 (not_3_out, d_ff_1_qn);
  D_Flip_Flop d_ff_2 (.D(d_ff_1_q), .clk(CLK_out), .Q(d_ff_2_q), .preset(not_3_out), .reset(not_4_out));  // open: Qn
  not not_4 (not_4_out, 1'b1);
  nand nand_1 (negWAIT, d_ff_1_qn, d_ff_2_q);
endmodule

module inc_8bit (
  input  [7:0] reg_in,
  output flag_n,
  output [7:0] inc_out,
  output flag_z,
  output flag_s,
  output flag_h,
  output flag_pv
);

  wire [7:1] undriven;

  Comparator comparator_1 (.a(reg_in), .b(8'h7f), .eq(flag_pv));  // open: gt, lt
  add_8bit add_8bit_1 (
    .Acc_1({undriven, 1'b1}), .reg_in(reg_in), .acc_out(inc_out), .flag_z(flag_z), .flag_s(flag_s),
    .flag_h(flag_h));  // open: out_3, out_4, out_6, flag_c, flag_pv

  assign flag_n = 1'b0;

  // Notes on the sheet:
  //   N is reset. C is not affected
  //   H is set if carry from bit 3; otherwise, it is reset. P/V is set if r was 7Fh before operation; otherwise, it is reset
  //   S is set if result is negative; otherwise, it is reset. Z is set if result is 0; otherwise, it is reset. 
endmodule

module add_8bit (
  input  [7:0] Acc_1,
  input  [7:0] reg_in,
  output [7:0] out_3,
  output [7:0] out_4,
  output [7:0] acc_out,
  output [7:0] out_6,
  output flag_z,
  output flag_s,
  output flag_h,
  output flag_c,
  output flag_pv
);

  Adder adder_1 (.a(reg_in), .b(Acc_1), .out(acc_out), .cout(flag_c));  // open: cin
  Adder #(.width(4)) adder_2 (.a(reg_in[3:0]), .b(Acc_1[3:0]), .cout(flag_h));  // open: out, cin
  Comparator comparator_1 (.a(acc_out), .b({8{1'b0}}), .eq(flag_z), .lt(flag_s));  // open: gt

  assign flag_pv = flag_c;
  assign out_3 = Acc_1;
  assign out_4 = reg_in;
  assign out_6 = acc_out;

  // Other names for the same wires on the sheet: Acc[7:0] = Acc_1

  // Notes on the sheet:
  //   P/V is set if overflow; otherwise, it is reset. N is reset. C is set if carry from bit 7; otherwise, it is reset.
  //   S is set if result is negative; otherwise, it is reset. Z is set if result is 0; otherwise, it is reset. H is set if carry from bit 3; otherwise, it is reset.
endmodule

module registers (
  input  [7:0] in_1,
  input  [7:0] in_2,
  input  [7:0] in_3,
  input  [7:0] in_4,
  input  [7:0] in_5,
  input  [7:0] in_6,
  input  [2:0] in_7,
  input  [7:0] in_8,
  input  in_9,
  output [7:0] out_10
);

  wire clock_1_out;
  wire [7:0] add_8bit_1_acc_out, multiplexer_1_out, register_1_q, register_2_q, register_3_q, register_4_q,
       register_5_q, register_6_q;

  Clock clock_1 (.out(clock_1_out));
  Register register_1 (.D(in_1), .clk(clock_1_out), .Q(register_1_q));  // open: en, clr
  Register register_2 (.D(in_3), .clk(clock_1_out), .Q(register_2_q));  // open: en, clr
  Register register_3 (.D(in_4), .clk(clock_1_out), .Q(register_3_q));  // open: en, clr
  Register register_4 (.D(in_5), .clk(clock_1_out), .Q(register_4_q));  // open: en, clr
  Register register_5 (.D(in_6), .clk(clock_1_out), .Q(register_5_q));  // open: en, clr
  Register register_6 (.D(in_8), .clk(clock_1_out), .Q(register_6_q));  // open: en, clr
  Multiplexer #(.select(3), .width(8)) multiplexer_1 (
    .in0(register_1_q), .in1(register_2_q), .in2(register_3_q), .in3(register_4_q), .in4(register_5_q),
    .in5(register_6_q), .in7(out_10), .out(multiplexer_1_out), .sel(in_7));  // open: in6
  add_8bit add_8bit_1 (
    .Acc_1(out_10), .reg_in(multiplexer_1_out), .acc_out(add_8bit_1_acc_out));  // open: out_3, out_4, out_6, flag_z, flag_s, flag_h, flag_c, flag_pv
  Register register_7 (.D(add_8bit_1_acc_out), .clk(clock_1_out), .Q(out_10), .clr(in_9));  // open: en
endmodule
